# Fritzing sketch GyroPlane-Client (saved by Fritzing 0.9.3b)
breadboards: 1

parts:
  Part2 = Arduino Nano (Rev3.0)
  Part3 = NCP1400 Step-Up Breakout
  Part4 = NRF24L01+ Breakout Board
  GY1 = GY-521 (MPU-6050) [form="♀ (female)" package=THT]
  Part5 = TP4056 Charger
  S1 = SPST Switch [package=switche-dpdt]
  Part6 = ws2812b [package="smd 2812b"]
  U1 = Voltage Regulator - 3.3V [package="TO220 [THT]"]
  C2 = Electrolytic Capacitor [capacitance=1000µF package="300 mil [THT, electrolytic]"]
  C3 = Electrolytic Capacitor [capacitance=1000µF package="300 mil [THT, electrolytic]"]
  U2 = LIPO-1000mAh [package=lipo-1000]

nets:
  GND: Part2.GND, Part4.GND, GY1.pin2, GY1.pin7, Part6.VSS
  N1: Part2.D2, GY1.pin8
  N2: Part2.D4, Part6.DIN
  N3: Part2.D7, Part4.CE
  N4: Part2.D8, Part4.CS
  N5: Part2.D11/MOSI, Part4.MOSI
  N6: Part2.D12/MISO, Part4.MISO
  N7: Part2.5V, Part3.VOUT, U1.input_voltage, C2.+
  N8: Part2.A5, GY1.pin3
  N9: Part2.A4, GY1.pin4
  N10: Part2.D13/SCK, Part4.SCK
  GND_2: Part3.GND, S1.S, U1.GND, C2.-, C3.-
  N11: Part3.VIN, Part5.IN-, Part5.BAT-, U2.+
  N12: Part4.VCC, U1.output_voltage, C3.+
  N13: GY1.pin1, Part6.VDD
  N14: Part5.IN+, Part5.BAT+, S1.P, U2.-

custom parts:
  GY-521 (MPU-6050): Placa GY-521 basada en conjunto de acelerómetro+giroscopios MPU-6050
